// Logisim project Unidade_Lógica_Aritmética_FINAL.circ as structural Verilog: 10 circuits, main circuit main
module main (
  input  [7:0] A,
  input  Cin,
  input  [7:0] B,
  input  [3:0] opcode,
  input  [2:0] in_5,
  input  [2:0] in_6,
  output [7:0] S
);

  wire [7:0] A_t, DESL__DIREITA, DESL__ESQUERDA;

  Shifter #(.shift("lr")) shifter_1 (.in(A_t), .\dist (in_5), .out(DESL__DIREITA));
  Shifter shifter_2 (.in(A_t), .\dist (in_6), .out(DESL__ESQUERDA));
  ULA ula_1 (.A(A), .Cin(Cin), .B(B), .opcode(opcode), .Smux(S));  // open: in_5, in_6, in_7, out_9
endmodule

module ULA (
  input  [7:0] A,
  input  Cin,
  input  [7:0] B,
  input  [3:0] opcode,
  input  [2:0] in_5,
  input  [2:0] in_6,
  input  [7:0] in_7,
  output [7:0] Smux,
  output [7:0] out_9
);

  wire Cout;
  wire [7:0] AND, DESL__DIREITA, DESL__ESQUERDA, MULTIPLICADOR, NAND, NOR, NOT, OR, SOMADOR, SUBTRATOR, XNOR,
       XOR;

  assign AND = A & B;  // AND_Gate and_1, 8 bits wide
  assign NAND = ~A & ~B;  // AND_Gate and_2, 8 bits wide
  assign OR = A | B;  // OR_Gate or_1, 8 bits wide
  assign NOT = ~A;  // NOT_Gate not_1, 8 bits wide
  Shifter #(.shift("lr")) shifter_1 (.in(A), .\dist (in_5), .out(DESL__DIREITA));
  Shifter shifter_2 (.in(A), .\dist (in_6), .out(DESL__ESQUERDA));
  Somador_8_bits somador_8_bits_1 (.Cin(Cin), .in_2(A), .B(B), .S(SOMADOR), .Cout(Cout));
  Multiplier multiplier_1 (.a(A), .b(B), .out(MULTIPLICADOR), .cin(in_7), .cout(out_9));
  assign XNOR = ~(~A ^ ~B);  // XNOR_Gate xnor_1, 8 bits wide
  assign XOR = A ^ B;  // XOR_Gate xor_1, 8 bits wide
  assign NOR = ~(A | B);  // NOR_Gate nor_1, 8 bits wide
  Subtrator_8_bits subtrator_8_bits_1 (.A(A), .B(B), .Cin(Cin), .S(SUBTRATOR), .Cout(Cout));
  Multiplexer #(.select(4), .width(8)) multiplexer_1 (
    .in1(XNOR), .in2(OR), .in3(DESL__DIREITA), .in4(XOR), .in5(MULTIPLICADOR), .in6(NOR), .in7(AND),
    .in9(SUBTRATOR), .in10(DESL__ESQUERDA), .in11(NAND), .in12(NOT), .in15(SOMADOR), .out(Smux), .sel(opcode));  // open: in0, in8, in13, in14, en
endmodule

// h+
module Meio_Somador (
  input  A,
  input  B,
  output S,
  output C
);

  xor xor_1 (S, A, B);
  and and_1 (C, A, B);
endmodule

// full+
module Somador_full (
  input  A,
  input  B,
  input  Cin,
  output S,
  output C
);

  wire meio_somador_1_c, meio_somador_1_s, meio_somador_2_c;

  Meio_Somador meio_somador_1 (.A(A), .B(B), .S(meio_somador_1_s), .C(meio_somador_1_c));
  Meio_Somador meio_somador_2 (.A(meio_somador_1_s), .B(Cin), .S(S), .C(meio_somador_2_c));
  or or_1 (C, meio_somador_1_c, meio_somador_2_c);
endmodule

module Somador_4_bits (
  input  A3,
  input  B3,
  input  Cin,
  input  A2,
  input  B2,
  input  A1,
  input  B1,
  input  A0,
  input  B0,
  output S3,
  output S2,
  output S1,
  output S0,
  output C0
);

  wire somador_full_1_c, somador_full_2_c, somador_full_3_c;

  Somador_full somador_full_1 (.A(A3), .B(B3), .Cin(Cin), .S(S3), .C(somador_full_1_c));
  Somador_full somador_full_2 (.A(A2), .B(B2), .Cin(somador_full_1_c), .S(S2), .C(somador_full_2_c));
  Somador_full somador_full_3 (.A(A1), .B(B1), .Cin(somador_full_2_c), .S(S1), .C(somador_full_3_c));
  Somador_full somador_full_4 (.A(A0), .B(B0), .Cin(somador_full_3_c), .S(S0), .C(C0));
endmodule

module Somador_8_bits (
  input  Cin,
  input  [7:0] in_2,
  input  [7:0] B,
  output [7:0] S,
  output Cout
);

  wire somador_4_bits_1_c0;

  Somador_4_bits somador_4_bits_1 (
    .A3(in_2[0]), .B3(B[0]), .Cin(Cin), .A2(in_2[1]), .B2(B[1]), .A1(in_2[2]), .B1(B[2]), .A0(in_2[3]),
    .B0(B[3]), .C0(somador_4_bits_1_c0), .S3(S[0]), .S2(S[1]), .S1(S[2]), .S0(S[3]));
  Somador_4_bits somador_4_bits_2 (
    .A3(in_2[4]), .B3(B[4]), .Cin(somador_4_bits_1_c0), .A2(in_2[5]), .B2(B[5]), .A1(in_2[6]), .B1(B[6]),
    .A0(in_2[7]), .B0(B[7]), .C0(Cout), .S3(S[4]), .S2(S[5]), .S1(S[6]), .S0(S[7]));
endmodule

// h-
module Meio_Subtrator (
  input  A,
  input  B,
  output S,
  output T
);

  and and_1 (T, ~A, B);  // AND_Gate
  xor xor_1 (S, B, A);
endmodule

// full-
module Subtrator_full (
  input  A,
  input  B,
  input  Cin,
  output S,
  output Cout
);

  wire meio_subtrator_1_s, meio_subtrator_1_t, meio_subtrator_2_t;

  Meio_Subtrator meio_subtrator_1 (.A(A), .B(B), .S(meio_subtrator_1_s), .T(meio_subtrator_1_t));
  Meio_Subtrator meio_subtrator_2 (.A(meio_subtrator_1_s), .B(Cin), .S(S), .T(meio_subtrator_2_t));
  or or_1 (Cout, meio_subtrator_1_t, meio_subtrator_2_t);
endmodule

module Subtrator_4_bits (
  input  A3,
  input  B3,
  input  Cin,
  input  A2,
  input  B2,
  input  A1,
  input  B1,
  input  A0,
  input  B0,
  output S3,
  output S2,
  output S1,
  output S0,
  output C0
);

  wire subtrator_full_1_cout, subtrator_full_2_cout, subtrator_full_3_cout;

  Subtrator_full subtrator_full_1 (.A(A3), .B(B3), .Cin(Cin), .S(S3), .Cout(subtrator_full_1_cout));
  Subtrator_full subtrator_full_2 (.A(A2), .B(B2), .Cin(subtrator_full_1_cout), .S(S2), .Cout(subtrator_full_2_cout));
  Subtrator_full subtrator_full_3 (.A(A1), .B(B1), .Cin(subtrator_full_2_cout), .S(S1), .Cout(subtrator_full_3_cout));
  Subtrator_full subtrator_full_4 (.A(A0), .B(B0), .Cin(subtrator_full_3_cout), .S(S0), .Cout(C0));

  // Notes on the sheet:
  //   bit mais significativo
endmodule

module Subtrator_8_bits (
  input  Cin,
  input  [7:0] A,
  input  [7:0] B,
  output [7:0] S,
  output Cout
);

  wire subtrator_4_bits_1_c0;

  Subtrator_4_bits subtrator_4_bits_1 (
    .A3(A[0]), .B3(B[0]), .Cin(Cin), .A2(A[1]), .B2(B[1]), .A1(A[2]), .B1(B[2]), .A0(A[3]), .B0(B[3]),
    .S3(S[0]), .S2(S[1]), .S1(S[2]), .S0(S[3]), .C0(subtrator_4_bits_1_c0));
  Subtrator_4_bits subtrator_4_bits_2 (
    .A3(A[4]), .B3(B[4]), .Cin(subtrator_4_bits_1_c0), .A2(A[5]), .B2(B[5]), .A1(A[6]), .B1(B[6]), .A0(A[7]),
    .B0(B[7]), .S3(S[4]), .S2(S[5]), .S1(S[6]), .S0(S[7]), .C0(Cout));
endmodule
