// Logisim project relatorio 1 somador completo.circ as structural Verilog
// h +
module meio_somador (
  input  A,
  input  B,
  output S,
  output C
);

  xor xor_1 (S, A, B);
  and and_1 (C, A, B);
endmodule

// full +
module somador_completo (
  input  A,
  input  B,
  input  Cin,
  output S,
  output Cout
);

  wire meio_somador_1_c, meio_somador_1_s, meio_somador_2_c;

  meio_somador meio_somador_1 (.A(A), .B(B), .S(meio_somador_1_s), .C(meio_somador_1_c));
  meio_somador meio_somador_2 (.A(meio_somador_1_s), .B(Cin), .S(S), .C(meio_somador_2_c));
  or or_1 (Cout, meio_somador_1_c, meio_somador_2_c);
endmodule

module somador_2_bits (
  input  A1,
  input  B1,
  input  Cin,
  input  A2,
  input  B2,
  output S1,
  output S2,
  output Cout
);

  wire somador_completo_1_cout;

  somador_completo somador_completo_1 (.A(A1), .B(B1), .Cin(Cin), .S(S1), .Cout(somador_completo_1_cout));
  somador_completo somador_completo_2 (.A(somador_completo_1_cout), .B(A2), .Cin(B2), .S(S2), .Cout(Cout));
endmodule
